# Fritzing sketch Ring_Board (saved by Fritzing 0.9.3b)
circuit board: 5.30098cm x 1.394cm
breadboards: 1

parts:
  Mod1 = seeeduino-xiao
  SW2 = Pushbutton [package="[THT]"]
  Dout = female pin header, 1 pin [form="♀ (female)"]
  GND = female pin header, 1 pin [form="♀ (female)"]
  SW1 = Pushbutton [package="[THT]"]
  5V = female pin header, 1 pin [form="♀ (female)"]
  C0 = Electrolytic Capacitor [capacitance=100µF voltage=16V package="100 mil [THT, electrolytic]"]
  C1 = Electrolytic Capacitor [capacitance=100µF voltage=16V package="100 mil [THT, electrolytic]"]

nets:
  N1: Mod1.D0, Dout.pin1
  N2: Mod1.D1, SW1.Pin_3, SW1.Pin_4
  N3: Mod1.D2, SW2.Pin_3, SW2.Pin_4
  N4: Mod1.GND, SW2.Pin_1, SW2.Pin_2, GND.pin1, SW1.Pin_1, SW1.Pin_2, C0.-, C1.-
  N5: Mod1.5V, 5V.pin1, C0.+, C1.+

custom parts:
  seeeduino-xiao: Seeeduino XIAO processor board.
